# Fritzing sketch Circuito_elevador-QRD-1114 (saved by Fritzing 0.9.3b)

parts:
  Part1 = Arduino Nano (Rev3.0) (ICSP)
  S4 = Pushbutton [package="[THT]"]
  S5 = Pushbutton [package="[THT]"]
  S6 = Pushbutton [package="[THT]"]
  R6 = Resistor [tolerance=±5% resistance=220 package="1206 [SMD]"]  # not connected
  R7 = Resistor [tolerance=±5% resistance=220 package="1206 [SMD]"]  # not connected
  R5 = Resistor [tolerance=±5% resistance=220 package="1206 [SMD]"]  # not connected
  S7 = H-Bridge with L298N
  U3 = Battery Holders [package=lipo-1100mAh]
  U2 = Battery Holders [package=lipo-1100mAh]
  7_Segment1 = 7 Segment Display
  R8 = Resistor [tolerance=±5% resistance=220 package="1206 [SMD]"]
  R9 = Resistor [tolerance=±5% resistance=220 package="1206 [SMD]"]
  R10 = Resistor [tolerance=±5% resistance=220 package="1206 [SMD]"]
  R11 = Resistor [tolerance=±5% resistance=220 package="1206 [SMD]"]
  R12 = Resistor [tolerance=±5% resistance=220 package="1206 [SMD]"]
  R13 = Resistor [tolerance=±5% resistance=220 package="1206 [SMD]"]
  R14 = Resistor [tolerance=±5% resistance=220 package="1206 [SMD]"]
  R15 = Resistor [tolerance=±5% resistance=220 package="1206 [SMD]"]
  R16 = Rotary Potentiometer (Small) [maximum_resistance=100kΩ package=THT]
  U4 = SWITCH-SPST-2 [package=switch-spst-vertical]  # not connected
  R17 = Resistor [tolerance=±5% resistance=10k package=THT]
  R18 = Resistor [tolerance=±5% resistance=220 package=THT]
  U5 = QRD1114 [package=qrd1114]
  U6 = QRD1114 [package=qrd1114]
  R19 = Resistor [tolerance=±5% resistance=10k package=THT]
  R20 = Resistor [tolerance=±5% resistance=220 package=THT]
  U7 = QRD1114 [package=qrd1114]
  R21 = Resistor [tolerance=±5% resistance=10k package=THT]
  R22 = Resistor [tolerance=±5% resistance=220 package=THT]

nets:
  N1: Part1.GND, 7_Segment1.common_cathode, R16.leg2, U5.E, U5.K
  N2: Part1.D2, R11.Pin_0
  N3: Part1.D3, R12.Pin_0
  N4: Part1.D4, R13.Pin_0
  N5: Part1.D6, S4.Pin_3, S4.Pin_4
  N6: Part1.D7, S5.Pin_3, S5.Pin_4
  N7: Part1.D8, S6.Pin_3, S6.Pin_4
  N8: Part1.D9, S7.IN1
  N9: Part1.D10, S7.IN2
  N10: Part1.D11/MOSI, S7.IN3
  N11: Part1.D12/MISO, R14.Pin_0
  N12: Part1.VIN, R16.leg1, R17.Pin_0, R18.Pin_0
  N13: Part1.A6, R16.wiper
  N14: Part1.A5, U7.C, R21.Pin_1
  N15: Part1.A4, U6.C, R19.Pin_1
  N16: Part1.A2, R10.Pin_0
  N17: Part1.A1, R8.Pin_0
  N18: Part1.A0, R9.Pin_0
  N19: Part1.D13/SCK, R15.Pin_0
  N20: S7.GND, U2.-
  N21: U3.-, U2.+
  N22: 7_Segment1.Segment_E, R12.Pin_1
  N23: 7_Segment1.Segment_D, R11.Pin_1
  N24: 7_Segment1.Segment_C, R10.Pin_1
  N25: 7_Segment1.Segment_DP, R15.Pin_1
  N26: 7_Segment1.Segment_B, R8.Pin_1
  N27: 7_Segment1.Segment_A, R9.Pin_1
  N28: 7_Segment1.Segment_F, R13.Pin_1
  N29: 7_Segment1.Segment_G, R14.Pin_1
  N30: R17.Pin_1, U5.C
  N31: R18.Pin_1, U5.A
  N32: U6.E, U6.K
  N33: U6.A, R20.Pin_1
  N34: U7.E, U7.K
  N35: U7.A, R22.Pin_1

custom parts:
  H-Bridge with L298N: h-bridge
